// Logisim project riscv.circ as structural Verilog: 21 circuits, main circuit RISCV32
module RISCV32 (
);

  wire and_1_out, and_2_out, and_4_out, and_7_out, and_9_out, and_10_out, AUIPC_q, branchpc_1_ifb,
       bypass_black_box_1_p3, clk, comparator_black_box_1_p4, comparator_black_box_1_p5,
       comparator_black_box_1_p6, DE_EX_regWE_q, DE_EX_set_q, DE_EX_shiftreg_q, DE_EX_useImm_q,
       decode_1_auipc, decode_1_ifj, decode_1_ifjalr, decode_1_ifload, decode_1_regwe, decode_1_set,
       decode_1_setsign, decode_1_shiftbyregval, decode_1_sig, decode_1_useimm, decode_1_zeroouta,
       ifbranch_1_ifb, ifjal_mem_q, ifjal_q, ifjalr_q, ifload_q, ifloadhar_q, loadhar_1_ifhar,
       multiplexer_4_out, not_1_out, not_2_out, not_3_out, not_4_out, not_5_out, not_6_out, not_7_out,
       not_8_out, not_9_out, not_10_out, not_11_out, or_1_out, or_2_out, or_3_out, registerfile_1_p3,
       set_signed_q, sig_q, ZeroOutA_q;
  wire [1:0] bypass_black_box_1_p7, bypass_black_box_1_p8, loadadd_1_bit;
  wire [3:0] and_5_out, and_6_out, bit_extender_1_out, bit_extender_2_out, DE_EX_ALUop_q, decode_1_aluop,
       decode_1_load_store, load_store_mem_q, load_store_q, ram_1_p4;
  wire [4:0] and_3_out, bit_extender_4_out, bypass_black_box_1_p4, DE_EX_rd_q, decode_1_rd, decode_1_rs1,
       decode_1_rs2, registerfile_1_p4, rs1_q, rs2_q;
  wire [5:0] and_8_out, bit_extender_3_out, branchhot_q, decode_1_branchhot;
  wire [19:0] loadadd_1_bit20;
  wire [31:0] bit_extender_5_out, Data_Store_q, DE_EX_A_q, DE_EX_B_q, DE_EX_imm_q, DE_EX_PC_q, decode_1_imm,
       EX_M_Result_q, execute_1_result, fetch_1_pcplus4, fetch_1_ram, IF_DE_instr_q, loadbyte_1_result,
       multiplexer_1_out, multiplexer_2_out, multiplexer_3_out, multiplexer_5_out, multiplexer_6_out,
       multiplexer_7_out, multiplexer_8_out, mux3to1_1_out_5, mux3to1_2_out_5, nop_1_res, PC4_q, PC_q,
       PCpl4_q, PCplus4_q, ram_1_p7, registerfile_1_p1, registerfile_1_p7, registerfile_1_p8,
       risc_vprogramrom_1_p2, store_1_re;

  Clock clock_1 (.out(clk));
  fetch fetch_1 (
    .clk(clk), .ifl(loadhar_1_ifhar), .PC(PC_q), .ifb(and_1_out), .Branch(multiplexer_5_out),
    .RAM(fetch_1_ram), .PCplus4(fetch_1_pcplus4));
  nop nop_1 (.ifzap(and_1_out), .res(nop_1_res));
  // RISC_VProgramROM risc_vprogramrom_1: pin names not known; wires that end beside it: fetch_1_ram, risc_vprogramrom_1_p2
  and and_1 (and_1_out, not_1_out, or_2_out);
  not not_1 (not_1_out, ifloadhar_q);
  Multiplexer #(.width(32), .enable("false")) multiplexer_1 (
    .in0(IF_DE_instr_q), .in1(nop_1_res), .out(multiplexer_1_out), .sel(and_1_out));
  Register #(.width(32)) IF_DE_instr (.D(risc_vprogramrom_1_p2), .clk(clk), .Q(IF_DE_instr_q));  // open: en, clr
  Register #(.width(32)) PC (.D(fetch_1_ram), .clk(clk), .Q(PC_q));  // open: en, clr
  Register #(.width(32)) PCplus4 (.D(fetch_1_pcplus4), .clk(clk), .Q(PCplus4_q));  // open: en, clr
  not not_2 (not_2_out, clk);
  Decode decode_1 (
    .instr(multiplexer_1_out), .Rs1(decode_1_rs1), .Rd(decode_1_rd), .Rs2(decode_1_rs2), .Imm(decode_1_imm),
    .useImm(decode_1_useimm), .ALUOp(decode_1_aluop), .regWE(decode_1_regwe), .set(decode_1_set),
    .shiftbyregval(decode_1_shiftbyregval), .setsign(decode_1_setsign), .AUIPC(decode_1_auipc),
    .ZeroOutA(decode_1_zeroouta), .load_store(decode_1_load_store), .ifj(decode_1_ifj),
    .ifjalr(decode_1_ifjalr), .branchhot(decode_1_branchhot), .ifload(decode_1_ifload), .sig(decode_1_sig));
  loadhar loadhar_1 (
    .ifload(ifload_q), .rd(DE_EX_rd_q), .rs1(decode_1_rs1), .rs2(decode_1_rs2), .ifhar(loadhar_1_ifhar));
  // RegisterFile registerfile_1: pin names not known; wires that end beside it: registerfile_1_p1, not_2_out, registerfile_1_p3, registerfile_1_p4, decode_1_rs1, decode_1_rs2, registerfile_1_p7, registerfile_1_p8
  not not_3 (not_3_out, loadhar_1_ifhar);
  assign bit_extender_1_out = {{3{not_3_out}}, not_3_out};  // Bit_Extender bit_extender_1
  assign bit_extender_2_out = {{3{not_4_out}}, not_4_out};  // Bit_Extender bit_extender_2
  not not_4 (not_4_out, and_2_out);
  assign bit_extender_3_out = {{5{not_5_out}}, not_5_out};  // Bit_Extender bit_extender_3
  not not_5 (not_5_out, and_2_out);
  not not_6 (not_6_out, ifloadhar_q);
  not not_7 (not_7_out, and_2_out);
  not not_8 (not_8_out, and_2_out);
  and and_2 (and_2_out, not_6_out, or_2_out);
  Register #(.width(32)) DE_EX_A (.D(registerfile_1_p7), .clk(clk), .Q(DE_EX_A_q));  // open: en, clr
  Register #(.width(32)) DE_EX_B (.D(registerfile_1_p8), .clk(clk), .Q(DE_EX_B_q));  // open: en, clr
  Register #(.width(5)) rs1 (.D(decode_1_rs1), .clk(clk), .Q(rs1_q));  // open: en, clr
  Register #(.width(5)) rs2 (.D(decode_1_rs2), .clk(clk), .Q(rs2_q));  // open: en, clr
  Register #(.width(5)) DE_EX_rd (.D(and_3_out), .clk(clk), .Q(DE_EX_rd_q));  // open: en, clr
  assign and_3_out = decode_1_rd & bit_extender_4_out;  // AND_Gate and_3, 5 bits wide
  Register #(.width(32)) DE_EX_imm (.D(decode_1_imm), .clk(clk), .Q(DE_EX_imm_q));  // open: en, clr
  Register #(.width(1)) DE_EX_useImm (.D(decode_1_useimm), .clk(clk), .Q(DE_EX_useImm_q));  // open: en, clr
  Register #(.width(4)) DE_EX_ALUop (.D(decode_1_aluop), .clk(clk), .Q(DE_EX_ALUop_q));  // open: en, clr
  Register #(.width(1)) DE_EX_regWE (.D(and_4_out), .clk(clk), .Q(DE_EX_regWE_q));  // open: en, clr
  and and_4 (and_4_out, decode_1_regwe, not_7_out);
  Register #(.width(1)) DE_EX_set (.D(decode_1_set), .clk(clk), .Q(DE_EX_set_q));  // open: en, clr
  Register #(.width(1)) DE_EX_shiftreg (.D(decode_1_shiftbyregval), .clk(clk), .Q(DE_EX_shiftreg_q));  // open: en, clr
  Register #(.width(1)) set_signed (.D(decode_1_setsign), .clk(clk), .Q(set_signed_q));  // open: en, clr
  Register #(.width(32)) DE_EX_PC (.D(PC_q), .clk(clk), .Q(DE_EX_PC_q));  // open: en, clr
  Register #(.width(1)) AUIPC (.D(decode_1_auipc), .clk(clk), .Q(AUIPC_q));  // open: en, clr
  Register #(.width(4)) load_store (.D(and_5_out), .clk(clk), .Q(load_store_q));  // open: en, clr
  assign and_5_out = bit_extender_1_out & and_6_out;  // AND_Gate and_5, 4 bits wide
  assign and_6_out = decode_1_load_store & bit_extender_2_out;  // AND_Gate and_6, 4 bits wide
  Register #(.width(1)) ifjal (.D(and_7_out), .clk(clk), .Q(ifjal_q));  // open: en, clr
  and and_7 (and_7_out, decode_1_ifj, not_8_out);
  Register #(.width(32)) PC4 (.D(PCplus4_q), .clk(clk), .Q(PC4_q));  // open: en, clr
  Register #(.width(6)) branchhot (.D(and_8_out), .clk(clk), .Q(branchhot_q));  // open: en, clr
  assign and_8_out = decode_1_branchhot & bit_extender_3_out;  // AND_Gate and_8, 6 bits wide
  Register #(.width(1)) ZeroOutA (.D(decode_1_zeroouta), .clk(clk), .Q(ZeroOutA_q));  // open: en, clr
  Register #(.width(1)) ifload (.D(and_9_out), .clk(clk), .Q(ifload_q));  // open: en, clr
  and and_9 (and_9_out, decode_1_ifload, not_9_out);
  not not_9 (not_9_out, and_2_out);
  Register #(.width(1)) sig (.D(decode_1_sig), .clk(clk), .Q(sig_q));  // open: en, clr
  Register #(.width(1)) ifjalr (.D(decode_1_ifjalr), .clk(clk), .Q(ifjalr_q));  // open: en, clr
  Register #(.width(1)) ifloadhar (.D(loadhar_1_ifhar), .clk(clk), .Q(ifloadhar_q));  // open: en, clr
  not not_10 (not_10_out, ifjalr_q);
  or or_1 (or_1_out, AUIPC_q, and_10_out, branchpc_1_ifb);
  and and_10 (and_10_out, ifjal_q, not_10_out);
  branchpc branchpc_1 (.branchhot(branchhot_q), .ifb(branchpc_1_ifb));
  // Bypass_Black_Box bypass_black_box_1: pin names not known; wires that end beside it: rs1_q, rs2_q, bypass_black_box_1_p3, bypass_black_box_1_p4, registerfile_1_p3, registerfile_1_p4, bypass_black_box_1_p7, bypass_black_box_1_p8
  not not_11 (not_11_out, loadhar_1_ifhar);
  assign bit_extender_4_out = {{4{not_11_out}}, not_11_out};  // Bit_Extender bit_extender_4
  MUX3to1 mux3to1_1 (
    .EX(DE_EX_A_q), .out_5(mux3to1_1_out_5), .WB(registerfile_1_p1), .ME(EX_M_Result_q),
    .Sel(bypass_black_box_1_p7));
  MUX3to1 mux3to1_2 (
    .EX(DE_EX_B_q), .out_5(mux3to1_2_out_5), .WB(registerfile_1_p1), .ME(EX_M_Result_q),
    .Sel(bypass_black_box_1_p8));
  Multiplexer #(.width(32), .enable("false")) multiplexer_2 (
    .in0(mux3to1_2_out_5), .in1(DE_EX_imm_q), .out(multiplexer_2_out), .sel(DE_EX_useImm_q));
  Multiplexer #(.width(32), .enable("false")) multiplexer_3 (
    .in0(multiplexer_2_out), .in1(mux3to1_2_out_5), .out(multiplexer_3_out), .sel(branchpc_1_ifb));
  Multiplexer #(.enable("false")) multiplexer_4 (
    .in0(set_signed_q), .in1(sig_q), .out(multiplexer_4_out), .sel(branchpc_1_ifb));
  // Comparator_Black_Box comparator_black_box_1: pin names not known; wires that end beside it: mux3to1_1_out_5, multiplexer_3_out, multiplexer_4_out, comparator_black_box_1_p4, comparator_black_box_1_p5, comparator_black_box_1_p6
  Execute execute_1 (
    .A(mux3to1_1_out_5), .B(mux3to1_2_out_5), .rB(rs2_q), .imm(DE_EX_imm_q), .useImm(DE_EX_useImm_q),
    .ALUop(DE_EX_ALUop_q), .shiftbyregval(DE_EX_shiftreg_q), .UsePC(or_1_out), .PC(DE_EX_PC_q),
    .branchhot(branchpc_1_ifb), .ZeroA(ZeroOutA_q), .result(execute_1_result));
  Multiplexer #(.width(32), .enable("false")) multiplexer_5 (
    .in0(execute_1_result), .in1(bit_extender_5_out), .out(multiplexer_5_out), .sel(DE_EX_set_q));
  assign bit_extender_5_out = {{31{1'b0}}, comparator_black_box_1_p6};  // Bit_Extender bit_extender_5
  ifbranch ifbranch_1 (
    .brachhot(branchhot_q), .greater(comparator_black_box_1_p4), .equal(comparator_black_box_1_p5),
    .less(comparator_black_box_1_p6), .ifb(ifbranch_1_ifb));
  or or_2 (or_2_out, ifjal_q, ifbranch_1_ifb);
  Register #(.width(32)) EX_M_Result (.D(multiplexer_5_out), .clk(clk), .Q(EX_M_Result_q));  // open: en, clr
  Register #(.width(5)) EX_M_rd (.D(DE_EX_rd_q), .clk(clk), .Q(bypass_black_box_1_p4));  // open: en, clr
  Register #(.width(1)) EX_M_regWE (.D(DE_EX_regWE_q), .clk(clk), .Q(bypass_black_box_1_p3));  // open: en, clr
  Register #(.width(32)) Data_Store (.D(mux3to1_2_out_5), .clk(clk), .Q(Data_Store_q));  // open: en, clr
  Register #(.width(4)) load_store_mem (.D(load_store_q), .clk(clk), .Q(load_store_mem_q));  // open: en, clr
  Register #(.width(1)) ifjal_mem (.D(ifjal_q), .clk(clk), .Q(ifjal_mem_q));  // open: en, clr
  Register #(.width(32)) PCpl4 (.D(PC4_q), .clk(clk), .Q(PCpl4_q));  // open: en, clr
  or or_3 (or_3_out, load_store_mem_q[2], load_store_mem_q[0]);
  store store_1 (.data(Data_Store_q), .ifwo(load_store_mem_q[0]), .re(store_1_re));
  loadadd loadadd_1 (.result(EX_M_Result_q), .bit20(loadadd_1_bit20), .\bit (loadadd_1_bit));
  // RAM ram_1: pin names not known; wires that end beside it: loadadd_1_bit20, store_1_re, load_store_mem_q[1], ram_1_p4, clk, load_store_mem_q[3], ram_1_p7
  bitselect bitselect_1 (.\bit (loadadd_1_bit), .ifword(or_3_out), .bitselect(ram_1_p4));
  Multiplexer #(.width(32), .enable("false")) multiplexer_6 (
    .in0(loadbyte_1_result), .in1(ram_1_p7), .out(multiplexer_6_out), .sel(load_store_mem_q[2]));
  loadbyte loadbyte_1 (.memin(ram_1_p7), .bitselect(loadadd_1_bit), .result(loadbyte_1_result));
  Multiplexer #(.width(32), .enable("false")) multiplexer_7 (
    .in0(EX_M_Result_q), .in1(multiplexer_6_out), .out(multiplexer_7_out), .sel(load_store_mem_q[3]));
  Multiplexer #(.width(32), .enable("false")) multiplexer_8 (
    .in0(multiplexer_7_out), .in1(PCpl4_q), .out(multiplexer_8_out), .sel(ifjal_mem_q));
  Register #(.width(32)) M_W_Result (.D(multiplexer_8_out), .clk(clk), .Q(registerfile_1_p1));  // open: en, clr
  Register #(.width(1)) M_W_regWE (.D(bypass_black_box_1_p3), .clk(clk), .Q(registerfile_1_p3));  // open: en, clr
  Register #(.width(5)) M_W_rd (.D(bypass_black_box_1_p4), .clk(clk), .Q(registerfile_1_p4));  // open: en, clr

  // Notes on the sheet:
  //   Notes:
  //   not to force you into using a template
  //   This is a working circuit for all of the table A instructions
  //   - Feel free to change the structure of this for any reason
  //   as it is to save you from repeating work you've done,
  //   - Behavior for table B instructions is undefined in this release circuit
  //   - This should pass the sanity check if you submit it as is
  //   contents of risc_vprogramrom_1 (hex, n*v repeats v):
  //   sw x1, 8(x0) addi x2, x8, 0
  //   Register Write Enable
  //   Okay to leave
  //   these outputs unused
endmodule

module Increment_PC (
  input  [31:0] in_1,
  output [31:0] out_2
);

  // Incrementer #(.width(30)) incrementer_1: pin names not known; wires that end beside it: in_1[31:2], out_2[31:2]

  assign out_2[1:0] = in_1[1:0];
endmodule

module Decode (
  input  [31:0] instr,
  output [4:0] Rs1,
  output [4:0] Rd,
  output [4:0] Rs2,
  output [31:0] Imm,
  output useImm,
  output [3:0] ALUOp,
  output regWE,
  output set,
  output shiftbyregval,
  output setsign,
  output AUIPC,
  output ZeroOutA,
  output [3:0] load_store,
  output ifj,
  output ifjalr,
  output [5:0] branchhot,
  output ifload,
  output sig
);

  wire decode_black_box_1_p6, jalorjalr_1_useimm, jalwrite_1_b, lorsbx_1_ifimm, or_1_out, or_4_out, undriven,
       undriven_2;
  wire [3:0] branch_1_alu, decode_black_box_1_p7, jalorjalr_1_aluop, lorsbx_1_alucode;
  wire [4:0] branch_1_rs1, branch_1_rs2, decode_black_box_1_p2, decode_black_box_1_p3, decode_black_box_1_p4,
       jalorjalr_1_rs1, jalorjalr_1_rs2, lorsbx_1_rd, lorsbx_1_rs1, lorsbx_1_rs2;
  wire [24:0] decode_black_box_1_p8;
  wire [31:0] branch_1_imm, decode_black_box_1_p5, jalorjalr_1_imm, lorsbx_1_imm;

  jalwrite jalwrite_1 (.c(or_1_out), .a0(instr[0]), .a1(instr[1]), .a2(instr[2]), .b(jalwrite_1_b));
  // Decode_Black_Box decode_black_box_1: pin names not known; wires that end beside it: instr, decode_black_box_1_p2, decode_black_box_1_p3, decode_black_box_1_p4, decode_black_box_1_p5, decode_black_box_1_p6, decode_black_box_1_p7, decode_black_box_1_p8[0], decode_black_box_1_p8[1], decode_black_box_1_p8[2], decode_black_box_1_p8[3], decode_black_box_1_p8[4], decode_black_box_1_p8[5], decode_black_box_1_p8[6], decode_black_box_1_p8[7], decode_black_box_1_p8[8], decode_black_box_1_p8[9], decode_black_box_1_p8[10], decode_black_box_1_p8[11], decode_black_box_1_p8[12], decode_black_box_1_p8[13], decode_black_box_1_p8[14], decode_black_box_1_p8[15], decode_black_box_1_p8[16], decode_black_box_1_p8[17], decode_black_box_1_p8[18], decode_black_box_1_p8[19], ZeroOutA, AUIPC, decode_black_box_1_p8[22], decode_black_box_1_p8[23], decode_black_box_1_p8[24], ifjalr, branchhot[0], branchhot[1], branchhot[2], branchhot[3], branchhot[4]
  or or_1 (or_1_out, instr[4], ~instr[5]);  // OR_Gate
  or or_2 (regWE, or_1_out, jalwrite_1_b);
  or or_3 (set, decode_black_box_1_p8[13], decode_black_box_1_p8[12], decode_black_box_1_p8[11], decode_black_box_1_p8[10]);
  or or_4 (or_4_out, branchhot[5], branchhot[4], branchhot[3], branchhot[2], branchhot[1], branchhot[0]);
  or or_5 (shiftbyregval, decode_black_box_1_p8[14], decode_black_box_1_p8[16], decode_black_box_1_p8[18]);
  or or_6 (setsign, decode_black_box_1_p8[11], decode_black_box_1_p8[10]);
  or or_7 (ifload, undriven_2, decode_black_box_1_p8[22]);
  storeload storeload_1 (
    .sw(decode_black_box_1_p8[23]), .sb(undriven), .lw(decode_black_box_1_p8[22]), .lb(undriven_2),
    .load_store(load_store));
  lorsbx lorsbx_1 (
    .instruction(instr), .immin(decode_black_box_1_p5), .rdin(decode_black_box_1_p4),
    .rs1in(decode_black_box_1_p2), .ifimmin(decode_black_box_1_p6), .aluopin(decode_black_box_1_p7),
    .lw(decode_black_box_1_p8[22]), .lb(undriven_2), .sw(decode_black_box_1_p8[23]), .sb(undriven),
    .rs2in(decode_black_box_1_p3), .imm(lorsbx_1_imm), .rd(lorsbx_1_rd), .rs1(lorsbx_1_rs1),
    .ifimm(lorsbx_1_ifimm), .alucode(lorsbx_1_alucode), .rs2(lorsbx_1_rs2));
  or or_8 (ifj, ifjalr, decode_black_box_1_p8[24]);
  jalorjalr jalorjalr_1 (
    .instr(instr), .rs1in(lorsbx_1_rs1), .rs2in(lorsbx_1_rs2), .rdin(lorsbx_1_rd), .immin(lorsbx_1_imm),
    .useimmin(lorsbx_1_ifimm), .aluopin(lorsbx_1_alucode), .jal(decode_black_box_1_p8[24]), .jalr(ifjalr),
    .rs1(jalorjalr_1_rs1), .rs2(jalorjalr_1_rs2), .rd(Rd), .imm(jalorjalr_1_imm),
    .useimm(jalorjalr_1_useimm), .aluop(jalorjalr_1_aluop));
  branch branch_1 (
    .Instr(instr), .ALU(branch_1_alu), .sig(sig), .Rs1(branch_1_rs1), .Rs2(branch_1_rs2), .Imm(branch_1_imm));
  Multiplexer #(.width(5), .enable("false")) multiplexer_1 (
    .in0(jalorjalr_1_rs1), .in1(branch_1_rs1), .out(Rs1), .sel(or_4_out));
  or or_9 (useImm, jalorjalr_1_useimm, or_4_out);
  Multiplexer #(.width(5), .enable("false")) multiplexer_2 (
    .in0(jalorjalr_1_rs2), .in1(branch_1_rs2), .out(Rs2), .sel(or_4_out));
  Multiplexer #(.width(32), .enable("false")) multiplexer_3 (
    .in0(jalorjalr_1_imm), .in1(branch_1_imm), .out(Imm), .sel(or_4_out));
  Multiplexer #(.width(4), .enable("false")) multiplexer_4 (
    .in0(jalorjalr_1_aluop), .in1(branch_1_alu), .out(ALUOp), .sel(or_4_out));

  // Notes on the sheet:
  //   Feel free to output the 1 hot if you want!
  //   Example of different ways to decode using what's given
endmodule

module Execute (
  input  [31:0] A,
  input  [31:0] B,
  input  [4:0] rB,
  input  [31:0] imm,
  input  useImm,
  input  [3:0] ALUop,
  input  shiftbyregval,
  input  UsePC,
  input  [31:0] PC,
  input  branchhot,
  input  ZeroA,
  output [31:0] result
);

  wire not_1_out;
  wire [4:0] multiplexer_3_out;
  wire [31:0] and_1_out, bit_extender_1_out, multiplexer_1_out, multiplexer_2_out, multiplexer_4_out,
       undriven;

  not not_1 (not_1_out, ZeroA);
  assign bit_extender_1_out = {{31{not_1_out}}, not_1_out};  // Bit_Extender bit_extender_1
  Multiplexer #(.width(32), .enable("false")) multiplexer_1 (.in0(B), .in1(imm), .out(multiplexer_1_out), .sel(useImm));
  Multiplexer #(.width(32), .enable("false")) multiplexer_2 (
    .in0(multiplexer_1_out), .in1(A), .out(multiplexer_2_out), .sel(shiftbyregval));
  Multiplexer #(.width(5), .enable("false")) multiplexer_3 (
    .in0(rB), .in1(B[4:0]), .out(multiplexer_3_out), .sel(shiftbyregval));
  Multiplexer #(.width(32), .enable("false")) multiplexer_4 (.in0(A), .in1(PC), .out(multiplexer_4_out), .sel(UsePC));
  assign and_1_out = multiplexer_4_out & bit_extender_1_out;  // AND_Gate and_1, 32 bits wide
  // ALU alu_1: pin names not known; wires that end beside it: and_1_out, multiplexer_2_out, ALUop, multiplexer_3_out
  Multiplexer #(.width(32), .enable("false")) multiplexer_5 (
    .in0(undriven), .in1(undriven), .out(result), .sel(branchhot));
endmodule

module MUX3to1 (
  input  [1:0] Sel,
  input  [31:0] EX,
  input  [31:0] WB,
  input  [31:0] ME,
  output [31:0] out_5
);

  wire [31:0] multiplexer_1_out;

  Multiplexer #(.width(32), .enable("false")) multiplexer_1 (.in0(EX), .in1(WB), .out(multiplexer_1_out), .sel(Sel[0]));
  Multiplexer #(.width(32), .enable("false")) multiplexer_2 (
    .in0(multiplexer_1_out), .in1(ME), .out(out_5), .sel(Sel[1]));
endmodule

module storeload (
  input  sw,
  input  sb,
  input  lw,
  input  lb,
  output [3:0] load_store
);

  or or_1 (load_store[1], sw, sb);
  or or_2 (load_store[3], lw, lb);

  assign {load_store[2], load_store[0]} = {lw, sw};
endmodule

module loadadd (
  input  [31:0] result,
  output [19:0] bit20,
  output [1:0] \bit 
);


  assign \bit  = result[1:0];
  assign bit20 = result[21:2];
endmodule

module borw (
  input  a1,
  input  a0,
  output b3,
  output b2,
  output b1,
  output b0
);

  wire not_1_out, not_2_out, not_3_out, not_4_out;

  and and_1 (b3, a1, a0);
  not not_1 (not_1_out, a0);
  not not_2 (not_2_out, a1);
  not not_3 (not_3_out, a1);
  not not_4 (not_4_out, a0);
  and and_2 (b2, a1, not_1_out);
  and and_3 (b1, not_2_out, a0);
  and and_4 (b0, not_3_out, not_4_out);
endmodule

module lorsbx (
  input  [31:0] instruction,
  input  [31:0] immin,
  input  [4:0] rdin,
  input  [4:0] rs1in,
  input  ifimmin,
  input  [3:0] aluopin,
  input  lw,
  input  lb,
  input  sw,
  input  sb,
  input  [4:0] rs2in,
  output [31:0] imm,
  output [4:0] rd,
  output [4:0] rs1,
  output ifimm,
  output [3:0] alucode,
  output [4:0] rs2
);

  wire or_1_out, or_2_out, or_3_out;
  wire [3:0] bit_extender_3_out;
  wire [31:0] bit_extender_1_out, bit_extender_2_out, multiplexer_1_out;

  or or_1 (or_1_out, lw, lb);
  or or_2 (or_2_out, sw, sb);
  assign bit_extender_1_out = {{20{instruction[31]}}, instruction[31:20]};  // Bit_Extender bit_extender_1
  or or_3 (or_3_out, or_1_out, or_2_out);
  assign bit_extender_2_out = {{20{instruction[31]}}, {instruction[31:25], instruction[11:7]}};  // Bit_Extender bit_extender_2
  Multiplexer #(.width(32), .enable("false")) multiplexer_1 (
    .in0(bit_extender_2_out), .in1(bit_extender_1_out), .out(multiplexer_1_out), .sel(or_1_out));
  Multiplexer #(.width(32), .enable("false")) multiplexer_2 (
    .in0(immin), .in1(multiplexer_1_out), .out(imm), .sel(or_3_out));
  Multiplexer #(.width(5), .enable("false")) multiplexer_3 (
    .in0(rdin), .in1(instruction[11:7]), .out(rd), .sel(or_3_out));
  Multiplexer #(.width(5), .enable("false")) multiplexer_4 (
    .in0(rdin), .in1(instruction[11:7]), .out(rd), .sel(or_3_out));
  Multiplexer #(.width(5), .enable("false")) multiplexer_5 (
    .in0(rs1in), .in1(instruction[19:15]), .out(rs1), .sel(or_3_out));
  Multiplexer #(.enable("false")) multiplexer_6 (.in0(ifimmin), .in1(or_3_out), .out(ifimm), .sel(or_3_out));
  assign bit_extender_3_out = {{3{1'b0}}, or_3_out};  // Bit_Extender bit_extender_3
  Multiplexer #(.width(5), .enable("false")) multiplexer_7 (
    .in0(rs2in), .in1(instruction[24:20]), .out(rs2), .sel(or_3_out));
  Multiplexer #(.width(4), .enable("false")) multiplexer_8 (
    .in0(aluopin), .in1({bit_extender_3_out[0], bit_extender_3_out[3:1]}), .out(alucode), .sel(or_3_out));
  Multiplexer #(.width(4), .enable("false")) multiplexer_9 (
    .in0(aluopin), .in1({bit_extender_3_out[0], bit_extender_3_out[3:1]}), .out(alucode), .sel(or_3_out));
endmodule

module bitselect (
  input  [1:0] \bit ,
  input  ifword,
  output [3:0] bitselect
);

  wire [3:0] bit_extender_1_out, borw_1_b0;

  borw borw_1 (
    .a1(\bit [1]), .a0(\bit [0]), .b3(borw_1_b0[3]), .b2(borw_1_b0[2]), .b1(borw_1_b0[1]), .b0(borw_1_b0[0]));
  assign bit_extender_1_out = {{3{ifword}}, ifword};  // Bit_Extender bit_extender_1
  assign bitselect = borw_1_b0 | bit_extender_1_out;  // OR_Gate or_1, 4 bits wide
endmodule

module loadbyte (
  input  [31:0] memin,
  input  [1:0] bitselect,
  output [31:0] result
);

  wire [31:0] bit_extender_1_out, bit_extender_2_out, bit_extender_3_out, bit_extender_4_out,
       multiplexer_1_out, multiplexer_2_out;

  assign bit_extender_1_out = {{24{memin[7]}}, memin[7:0]};  // Bit_Extender bit_extender_1
  assign bit_extender_2_out = {{24{memin[15]}}, memin[15:8]};  // Bit_Extender bit_extender_2
  assign bit_extender_3_out = {{24{memin[23]}}, memin[23:16]};  // Bit_Extender bit_extender_3
  assign bit_extender_4_out = {{24{memin[31]}}, memin[31:24]};  // Bit_Extender bit_extender_4
  Multiplexer #(.width(32), .enable("false")) multiplexer_1 (
    .in0(bit_extender_1_out), .in1(bit_extender_2_out), .out(multiplexer_1_out), .sel(bitselect[0]));
  Multiplexer #(.width(32), .enable("false")) multiplexer_2 (
    .in0(bit_extender_3_out), .in1(bit_extender_4_out), .out(multiplexer_2_out), .sel(bitselect[0]));
  Multiplexer #(.width(32), .enable("false")) multiplexer_3 (
    .in0(multiplexer_1_out), .in1(multiplexer_2_out), .out(result), .sel(bitselect[1]));
endmodule

module jalorjalr (
  input  [31:0] instr,
  input  [4:0] rs1in,
  input  [4:0] rs2in,
  input  [4:0] rdin,
  input  [31:0] immin,
  input  useimmin,
  input  [3:0] aluopin,
  input  jal,
  input  jalr,
  output [4:0] rs1,
  output [4:0] rs2,
  output [4:0] rd,
  output [31:0] imm,
  output useimm,
  output [3:0] aluop
);

  wire [0:0] not_1_out;
  wire [3:2] not_2_out;
  wire [4:0] and_1_out, bit_extender_3_out;
  wire [31:0] bit_extender_1_out, bit_extender_2_out, multiplexer_1_out;

  or or_1 (not_2_out[3], jal, jalr);
  assign bit_extender_1_out = {{20{instr[31]}}, instr[31:20]};  // Bit_Extender bit_extender_1
  assign bit_extender_2_out = {{11{instr[31]}}, {instr[31], instr[19:12], instr[20], instr[30:21], not_1_out[0]}};  // Bit_Extender bit_extender_2
  assign bit_extender_3_out = {{4{jalr}}, jalr};  // Bit_Extender bit_extender_3
  assign and_1_out = bit_extender_3_out & instr[19:15];  // AND_Gate and_1, 5 bits wide
  Multiplexer #(.width(32), .enable("false")) multiplexer_1 (
    .in0(bit_extender_2_out), .in1(bit_extender_1_out), .out(multiplexer_1_out), .sel(jalr));
  not not_1 (not_1_out[0], not_2_out[3]);
  Multiplexer #(.width(5), .enable("false")) multiplexer_2 (
    .in0(rs1in), .in1(and_1_out), .out(rs1), .sel(not_2_out[3]));
  Multiplexer #(.width(5), .enable("false")) multiplexer_3 (
    .in0(rdin), .in1(instr[11:7]), .out(rd), .sel(not_2_out[3]));
  Multiplexer #(.width(32), .enable("false")) multiplexer_4 (
    .in0(immin), .in1(multiplexer_1_out), .out(imm), .sel(not_2_out[3]));
  or or_2 (useimm, useimmin, not_2_out[3]);
  not not_2 (not_2_out[2], not_2_out[3]);
  Multiplexer #(.width(4), .enable("false")) multiplexer_5 (
    .in0(aluopin), .in1({not_2_out, {2{not_2_out[2]}}}), .out(aluop), .sel(not_2_out[3]));

  assign rs2 = rs2in;
endmodule

module jalwrite (
  input  c,
  input  a0,
  input  a1,
  input  a2,
  output b
);

  wire and_1_out;

  and and_1 (and_1_out, a0, a1, a2);
  or or_1 (b, and_1_out, c);
endmodule

module fetch (
  input  clk,
  input  ifl,
  input  [31:0] PC,
  input  ifb,
  input  [31:0] Branch,
  output [31:0] RAM,
  output [31:0] PCplus4
);

  wire [31:0] multiplexer_1_out, multiplexer_2_out;

  Register #(.width(32), .trigger("falling")) register_1 (.D(multiplexer_1_out), .clk(clk), .Q(RAM));  // open: en, clr
  Multiplexer #(.width(32), .enable("false")) multiplexer_1 (
    .in0(multiplexer_2_out), .in1(Branch), .out(multiplexer_1_out), .sel(ifb));
  Multiplexer #(.width(32), .enable("false")) multiplexer_2 (
    .in0(PCplus4), .in1(PC), .out(multiplexer_2_out), .sel(ifl));
  Increment_PC increment_pc_1 (.in_1(RAM), .out_2(PCplus4));
endmodule

module branch (
  input  [31:0] Instr,
  output [3:0] ALU,
  output sig,
  output [4:0] Rs1,
  output [4:0] Rs2,
  output [31:0] Imm
);

  not not_1 (sig, Instr[13]);
  assign Imm = {{19{Instr[31]}}, {Instr[31], Instr[7], Instr[30:25], Instr[11:8], Instr[2]}};  // Bit_Extender bit_extender_1

  assign ALU = {Instr[6], {3{Instr[2]}}};
  assign Rs1 = Instr[19:15];
  assign Rs2 = Instr[24:20];
endmodule

module luhar (
  input  [4:0] rs1in,
  input  [4:0] rs2in,
  input  [4:0] rdin,
  input  [3:0] opin,
  input  ifl,
  output [4:0] rs1,
  output [4:0] rs2,
  output [4:0] rd,
  output [3:0] op
);

  wire not_1_out;
  wire [3:0] bit_extender_2_out;
  wire [4:0] bit_extender_1_out;

  not not_1 (not_1_out, ifl);
  assign bit_extender_1_out = {{4{not_1_out}}, not_1_out};  // Bit_Extender bit_extender_1
  assign bit_extender_2_out = {{3{1'b0}}, ifl};  // Bit_Extender bit_extender_2
  assign rs1 = rs1in & bit_extender_1_out;  // AND_Gate and_1, 5 bits wide
  assign rs2 = rs2in & bit_extender_1_out;  // AND_Gate and_2, 5 bits wide
  assign rd = rdin & bit_extender_1_out;  // AND_Gate and_3, 5 bits wide
  Multiplexer #(.width(4), .enable("false")) multiplexer_1 (
    .in0(opin), .in1({bit_extender_2_out[0], bit_extender_2_out[3:1]}), .out(op), .sel(ifl));
endmodule

module loadhar (
  input  ifload,
  input  [4:0] rd,
  input  [4:0] rs1,
  input  [4:0] rs2,
  output ifhar
);

  wire and_1_out, and_2_out, and_3_out, not_1_out, not_2_out, or_1_out, or_2_out, or_3_out;
  wire [4:0] xor_1_out, xor_2_out;

  assign xor_1_out = rd ^ rs1;  // XOR_Gate xor_1, 5 bits wide
  and and_1 (and_1_out, ~rd[0], ~rd[1], ~rd[2], ~rd[3], ~rd[4]);  // AND_Gate
  or or_1 (or_1_out, xor_1_out[0], xor_1_out[1], xor_1_out[2], xor_1_out[3], xor_1_out[4]);
  assign xor_2_out = rd ^ rs2;  // XOR_Gate xor_2, 5 bits wide
  not not_1 (not_1_out, or_1_out);
  or or_2 (or_2_out, xor_2_out[0], xor_2_out[1], xor_2_out[2], xor_2_out[3], xor_2_out[4]);
  not not_2 (not_2_out, or_2_out);
  and and_2 (and_2_out, ~and_1_out, not_1_out);  // AND_Gate
  and and_3 (and_3_out, ~and_1_out, not_2_out);  // AND_Gate
  or or_3 (or_3_out, and_2_out, and_3_out);
  and and_4 (ifhar, ifload, or_3_out);
endmodule

module branchpc (
  input  [5:0] branchhot,
  output ifb
);

  or or_1 (ifb, branchhot[0], branchhot[1], branchhot[2], branchhot[3], branchhot[4], branchhot[5]);
endmodule

module ifbranch (
  input  [5:0] brachhot,
  input  greater,
  input  equal,
  input  less,
  output ifb
);

  wire and_1_out, and_2_out, and_3_out, and_4_out, and_5_out, and_6_out, not_1_out, or_1_out;

  and and_1 (and_1_out, brachhot[0], equal);
  and and_2 (and_2_out, brachhot[1], not_1_out);
  not not_1 (not_1_out, equal);
  and and_3 (and_3_out, brachhot[2], less);
  and and_4 (and_4_out, brachhot[3], or_1_out);
  or or_1 (or_1_out, equal, greater);
  and and_5 (and_5_out, brachhot[4], less);
  and and_6 (and_6_out, brachhot[5], or_1_out);
  or or_2 (ifb, and_1_out, and_2_out, and_3_out, and_4_out, and_5_out, and_6_out);

  // Notes on the sheet:
  //   BEQ
  //   BNE
  //   BLT
  //   BGE
  //   BGEU
  //   BLTU
endmodule

module store (
  input  [31:0] data,
  input  ifwo,
  output [31:0] re
);

  Multiplexer #(.width(32), .enable("false")) multiplexer_1 (
    .in0({data[7:0], data[7:0], data[7:0], data[7:0]}), .in1(data), .out(re), .sel(ifwo));
endmodule

module nop (
  input  ifzap,
  output [31:0] res
);

  not not_1 (res[3], ifzap);
  assign res[31:5] = {{26{res[3]}}, res[3]};  // Bit_Extender bit_extender_1

  assign {res[4], res[2:0]} = {ifzap, res[3], {2{ifzap}}};
endmodule
